// Logisim project And16.circ as structural Verilog: 1 circuit, main circuit main
module main (
  input  [15:0] in_1,
  input  [15:0] in_2,
  output [15:0] out_3
);

  assign out_3 = in_1 & in_2;  // AND_Gate and_1, 16 bits wide
endmodule
