// Logisim project DMux8Way.circ as structural Verilog: 1 circuit, main circuit main
module main (
  input  in_1,
  input  [2:0] in_2,
  output out_3,
  output out_4,
  output out_5,
  output out_6,
  output out_7,
  output out_8,
  output out_9,
  output out_10
);

  wire demultiplexer_1_out0, demultiplexer_1_out1, demultiplexer_1_out2, demultiplexer_1_out3;

  Demultiplexer #(.select(2)) demultiplexer_1 (
    .out0(demultiplexer_1_out0), .out1(demultiplexer_1_out1), .out2(demultiplexer_1_out2),
    .out3(demultiplexer_1_out3), .in(in_1), .sel(in_2[1:0]));  // open: en
  Demultiplexer demultiplexer_2 (.out0(out_3), .out1(out_4), .in(demultiplexer_1_out0), .sel(in_2[2]));  // open: en
  Demultiplexer demultiplexer_3 (.out0(out_5), .out1(out_6), .in(demultiplexer_1_out1), .sel(in_2[2]));  // open: en
  Demultiplexer demultiplexer_4 (.out0(out_7), .out1(out_8), .in(demultiplexer_1_out2), .sel(in_2[2]));  // open: en
  Demultiplexer demultiplexer_5 (.out0(out_9), .out1(out_10), .in(demultiplexer_1_out3), .sel(in_2[2]));  // open: en
endmodule
