// Logisim project Mux.circ as structural Verilog: 1 circuit, main circuit main
module main (
  input  a,
  input  sel,
  input  b,
  input  sel_2,
  output a_2,
  output b_2
);

  wire and_1_out, and_2_out, not_1_out, not_2_out, or_1_out;

  not not_1 (not_1_out, sel);
  and and_1 (and_1_out, a, not_1_out);
  and and_2 (and_2_out, sel, b);
  or or_1 (or_1_out, and_1_out, and_2_out);
  not not_2 (not_2_out, sel_2);
  and and_3 (a_2, or_1_out, not_2_out);
  and and_4 (b_2, or_1_out, sel_2);

  // Notes on the sheet:
  //   Mux
  //   in
  //   DMux
endmodule
