// Logisim project Xor.circ as structural Verilog: 1 circuit, main circuit main
module main (
);

  wire and_1_out, and_2_out, not_1_out, not_2_out, undriven, undriven_2;

  not not_1 (not_1_out, undriven_2);
  not not_2 (not_2_out, undriven);
  and and_1 (and_1_out, undriven_2, not_2_out);
  and and_2 (and_2_out, not_1_out, undriven);
  // OR_Gate or_1 has open pins: in1=and_1_out, in3=and_2_out, out=open
endmodule
