// Logisim project ALU.circ as structural Verilog: 1 circuit, main circuit main
module main (
  input  [15:0] in_1,
  input  zx,
  input  [15:0] in_3,
  input  nx,
  input  zy,
  input  f,
  input  no,
  input  ny
);

  wire [15:0] adder_1_out, and_1_out, and_2_out, and_3_out, multiplexer_1_out, multiplexer_2_out,
       multiplexer_3_out, multiplexer_4_out, multiplexer_5_out, multiplexer_6_out, not_1_out, not_2_out,
       not_3_out, not_4_out, not_5_out;

  assign not_1_out = ~in_1;  // NOT_Gate not_1, 16 bits wide
  assign not_2_out = ~in_3;  // NOT_Gate not_2, 16 bits wide
  assign and_1_out = in_1 & not_1_out;  // AND_Gate and_1, 16 bits wide
  assign and_2_out = in_3 & not_2_out;  // AND_Gate and_2, 16 bits wide
  Multiplexer #(.width(16)) multiplexer_1 (.in0(in_1), .in1(and_1_out), .out(multiplexer_1_out), .sel(zx));  // open: en
  Multiplexer #(.width(16)) multiplexer_2 (.in0(in_3), .in1(and_2_out), .out(multiplexer_2_out), .sel(zy));  // open: en
  assign not_3_out = ~multiplexer_1_out;  // NOT_Gate not_3, 16 bits wide
  assign not_4_out = ~multiplexer_2_out;  // NOT_Gate not_4, 16 bits wide
  Multiplexer #(.width(16)) multiplexer_3 (
    .in0(multiplexer_1_out), .in1(not_3_out), .out(multiplexer_3_out), .sel(nx));  // open: en
  Multiplexer #(.width(16)) multiplexer_4 (
    .in0(multiplexer_2_out), .in1(not_4_out), .out(multiplexer_4_out), .sel(ny));  // open: en
  Adder #(.width(16)) adder_1 (.a(multiplexer_3_out), .b(multiplexer_4_out), .out(adder_1_out));  // open: cin, cout
  assign and_3_out = multiplexer_3_out & multiplexer_4_out;  // AND_Gate and_3, 16 bits wide
  Multiplexer #(.width(16)) multiplexer_5 (
    .in0(and_3_out), .in1(adder_1_out), .out(multiplexer_5_out), .sel(f));  // open: en
  assign not_5_out = ~multiplexer_5_out;  // NOT_Gate not_5, 16 bits wide
  Multiplexer #(.width(16)) multiplexer_6 (
    .in0(multiplexer_5_out), .in1(not_5_out), .out(multiplexer_6_out), .sel(no));  // open: en

  // Notes on the sheet:
  //   x
  //   y
endmodule
