// Logisim project Add16.circ as structural Verilog: 1 circuit, main circuit main
module main (
  input  in_1,
  input  in_2,
  input  in_3,
  input  in_4,
  input  in_5,
  output out_6,
  output out_7
);

  wire and_1_out, and_2_out, and_3_out, and_4_out, or_1_out, or_2_out, xor_1_out, xor_3_out;

  xor xor_1 (xor_1_out, in_1, in_3);
  and and_1 (and_1_out, in_1, in_3);
  xor xor_2 (out_6, xor_1_out, in_5);
  and and_2 (and_2_out, xor_1_out, in_5);
  or or_1 (or_1_out, and_2_out, and_1_out);
  xor xor_3 (xor_3_out, in_2, in_4);
  and and_3 (and_3_out, in_2, in_4);
  xor xor_4 (out_7, xor_3_out, or_1_out);
  and and_4 (and_4_out, xor_3_out, or_1_out);
  or or_2 (or_2_out, and_4_out, and_3_out);
endmodule
