// Logisim project FullAdder.circ as structural Verilog: 1 circuit, main circuit main
module main (
  input  a,
  input  b,
  input  c,
  output sum,
  output carry
);

  wire and_1_out, and_2_out, xor_1_out;

  xor xor_1 (xor_1_out, a, b);
  and and_1 (and_1_out, a, b);
  xor xor_2 (sum, xor_1_out, c);
  and and_2 (and_2_out, xor_1_out, c);
  or or_1 (carry, and_2_out, and_1_out);

  // Notes on the sheet:
  //   HalfAdder
  //   FullAdder
  //   HalfAdder
endmodule
